// Logisim project POTEC_PLEWA_ZADARA.circ as structural Verilog: 2 circuits, main circuit main
module main (
  input  [3:0] X
);

  wire dec7_1_a, dec7_1_b, dec7_1_c, dec7_1_d, dec7_1_e, dec7_1_f, dec7_1_g;

  dec7 dec7_1 (.x(X), .a(dec7_1_a), .b(dec7_1_b), .c(dec7_1_c), .d(dec7_1_d), .e(dec7_1_e), .f(dec7_1_f), .g(dec7_1_g));
  _7_Segment_Display u_7_segment_display_1 (
    .g(dec7_1_g), .f(dec7_1_f), .a(dec7_1_a), .b(dec7_1_b), .e(dec7_1_e), .d(dec7_1_d), .c(dec7_1_c));  // open: dp
endmodule

module dec7 (
  input  [3:0] x,
  output a,
  output b,
  output c,
  output d,
  output e,
  output f,
  output g
);

  wire and_2_out, and_3_out, and_4_out, and_5_out, and_6_out, and_7_out, and_8_out, not_1_out, not_2_out,
       not_3_out, or_2_out, or_3_out, xnor_1_out, xnor_2_out, xnor_3_out, xor_1_out;

  not not_1 (not_1_out, x[2]);
  not not_2 (not_2_out, x[1]);
  not not_3 (not_3_out, x[0]);
  xnor xnor_1 (xnor_1_out, x[2], x[0]);
  xnor xnor_2 (xnor_2_out, x[1], x[0]);
  or or_1 (c, not_2_out, x[2], x[0]);
  or or_2 (or_2_out, not_3_out, not_1_out);
  xnor xnor_3 (xnor_3_out, x[2], x[0]);
  and and_1 (e, not_3_out, or_3_out);
  or or_3 (or_3_out, not_1_out, x[1]);
  and and_2 (and_2_out, x[2], not_2_out);
  and and_3 (and_3_out, x[3], not_2_out);
  and and_4 (and_4_out, x[2], not_3_out);
  and and_5 (and_5_out, not_2_out, not_3_out);
  and and_6 (and_6_out, x[1], not_3_out);
  xor xor_1 (xor_1_out, x[2], x[1]);
  or or_4 (a, x[3], x[1], xnor_1_out);
  or or_5 (b, not_1_out, xnor_2_out);
  and and_7 (and_7_out, x[1], or_2_out);
  and and_8 (and_8_out, not_2_out, xnor_3_out);
  or or_6 (f, and_2_out, and_3_out, and_4_out, and_5_out);
  or or_7 (g, and_6_out, xor_1_out, x[3]);
  or or_8 (d, x[3], and_7_out, and_8_out);
endmodule
