// Logisim project POTEC_PLEWA_ZADARA2.circ as structural Verilog: 2 circuits, main circuit main
module main (
  input  [3:0] a,
  input  [3:0] b,
  input  [3:0] c,
  input  [3:0] d,
  input  [3:0] e,
  input  [3:0] f,
  output [3:0] x,
  output [3:0] y,
  output [3:0] z,
  output [3:0] m,
  output [3:0] n,
  output [3:0] k
);

  wire [3:0] b0_x, b0_y, b1_x, b1_y, b2_x, b2_y, b3_x, b3_y, b4_x, b4_y, b5_x, b5_y, b6_y, b7_x, b7_y, b8_y,
       b9_x, b10_y;

  comp b0 (.a(a), .b(b), .x(b0_x), .y(b0_y));
  comp b1 (.a(c), .b(d), .x(b1_x), .y(b1_y));
  comp b2 (.a(e), .b(f), .x(b2_x), .y(b2_y));
  comp b3 (.a(b0_x), .b(b1_x), .x(b3_x), .y(b3_y));
  comp b4 (.a(b0_y), .b(b1_y), .x(b4_x), .y(b4_y));
  comp b5 (.a(b3_y), .b(b4_x), .x(b5_x), .y(b5_y));
  comp b6 (.a(b3_x), .b(b2_x), .x(x), .y(b6_y));
  comp b7 (.a(b5_x), .b(b2_y), .x(b7_x), .y(b7_y));
  comp b8 (.a(b7_x), .b(b6_y), .x(y), .y(b8_y));
  comp b9 (.a(b4_y), .b(b7_y), .x(b9_x), .y(k));
  comp b10 (.a(b5_y), .b(b8_y), .x(z), .y(b10_y));
  comp b11 (.a(b9_x), .b(b10_y), .x(m), .y(n));

  // Notes on the sheet:
  //   0
  //   5
  //   1
  //   2
  //   3
  //   4
  //   0
  //   t0
  //   1
  //   t1
  //   t2
  //   2
  //   3
  //   t3
  //   4
  //   t4
  //   5
  //   t5
  //   0
  //   t6
  //   2
  //   t7
  //   1
  //   t8
  //   3
  //   t9
  //   1
  //   t10
  //   2
  //   t11
  //   0
  //   x
  //   4
  //   t12
  //   1
  //   t13
  //   5
  //   t14
  //   1
  //   y
  //   4
  //   t15
  //   3
  //   t16
  //   5
  //   k
  //   2
  //   z
  //   4
  //   t17
  //   3
  //   m
  //   n
  //   4
endmodule

module comp (
  input  [3:0] a,
  input  [3:0] b,
  output [3:0] x,
  output [3:0] y
);

  wire comparator_1_gt;

  Comparator #(.mode("unsigned"), .width(4)) comparator_1 (.a(a), .b(b), .gt(comparator_1_gt));  // open: eq, lt
  Multiplexer #(.width(4)) multiplexer_1 (.in0(a), .in1(b), .out(x), .sel(comparator_1_gt));
  Multiplexer #(.width(4)) multiplexer_2 (.in0(b), .in1(a), .out(y), .sel(comparator_1_gt));
endmodule
